// Logisim project cpu.circ as structural Verilog: 1 circuit, main circuit cpu
module cpu (
  input  clk,
  input  [31:0] Instruction,
  input  [31:0] MemReadData,
  output [31:0] MemAddress,
  output [31:0] ProgramCounter,
  output [31:0] ra,
  output [31:0] sp,
  output [31:0] t0,
  output [31:0] t1,
  output [31:0] t2,
  output [31:0] s0,
  output [31:0] s1,
  output [31:0] a0,
  output [3:0] MemWriteMask,
  output [31:0] MemWriteData
);

  wire A, B, BrEq, BrLt, BrUn, MemWEn, PCSel, RegWEn;
  wire [1:0] WBSel;
  wire [2:0] ImmSel;
  wire [3:0] ALUSel;
  wire [31:0] Imm, Mem, multiplexer_1_out, multiplexer_2_out, multiplexer_3_out, multiplexer_4_out,
       PastInstruction, PC4, PC4Pipelined, ProgramCounter_t, RD, RS1, RS2;

  Adder #(.width(32)) adder_1 (.a(ProgramCounter), .b(32'h4), .out(PC4));  // open: cin, cout
  Multiplexer #(.width(32)) multiplexer_1 (.in0(PC4), .in1(MemAddress), .out(multiplexer_1_out), .sel(PCSel));
  Register #(.width(32)) PC (.D(multiplexer_1_out), .clk(clk), .Q(ProgramCounter));  // open: en, clr
  Multiplexer #(.width(32)) multiplexer_2 (.in0(Instruction), .in1(32'h13), .out(multiplexer_2_out), .sel(PCSel));
  Register #(.width(32)) register_1 (.D(multiplexer_2_out), .clk(clk), .Q(PastInstruction));  // open: en, clr
  Register #(.width(32)) register_2 (.D(ProgramCounter), .clk(clk), .Q(ProgramCounter_t));  // open: en, clr
  Register #(.width(32)) register_3 (.D(PC4), .clk(clk), .Q(PC4Pipelined));  // open: en, clr
  control_logic control_logic_1 (
    .Instruction(PastInstruction), .BrEq(BrEq), .BrLt(BrLt), .PCSel(PCSel), .RegWEn(RegWEn), .ImmSel(ImmSel),
    .BrUn(BrUn), .ASel(A), .BSel(B), .ALUSel(ALUSel), .MemWEn(MemWEn), .WBSel(WBSel));
  regfile regfile_1 (
    .ReadIndex1(PastInstruction[19:15]), .ReadIndex2(PastInstruction[24:20]),
    .WriteIndex(PastInstruction[11:7]), .WriteData(RD), .RegWEn(RegWEn), .clk(clk), .ra(ra), .sp(sp),
    .t0(t0), .t1(t1), .t2(t2), .s0(s0), .s1(s1), .a0(a0), .ReadData1(RS1), .ReadData2(RS2));
  imm_gen imm_gen_1 (.Instruction(PastInstruction), .ImmSel(ImmSel), .Immediate(Imm));
  Multiplexer #(.width(32)) multiplexer_3 (.in0(RS1), .in1(ProgramCounter_t), .out(multiplexer_3_out), .sel(A));
  Multiplexer #(.width(32)) multiplexer_4 (.in0(RS2), .in1(Imm), .out(multiplexer_4_out), .sel(B));
  alu alu_1 (.A(multiplexer_3_out), .B(multiplexer_4_out), .ALUSel(ALUSel), .ALUResult(MemAddress));
  branch_comp branch_comp_1 (.BrData1(RS1), .BrData2(RS2), .BrUn(BrUn), .BrEq(BrEq), .BrLt(BrLt));
  partial_store partial_store_1 (
    .Instruction(PastInstruction), .MemAddress(MemAddress), .DataFromReg(RS2), .MemWEn(MemWEn),
    .MemWriteMask(MemWriteMask), .DataToMem(MemWriteData));
  partial_load partial_load_1 (
    .Instruction(PastInstruction), .MemAddress(MemAddress), .DataFromMem(MemReadData), .DataToReg(Mem));
  Multiplexer #(.select(2), .width(32)) multiplexer_5 (
    .in0(Mem), .in1(MemAddress), .in2(PC4Pipelined), .out(RD), .sel(WBSel));  // open: in3

  // Other names for the same wires on the sheet: ALURes[31:0] = MemAddress; PCVal[31:0] = ProgramCounter

  // Notes on the sheet:
  //   To IMEM
  //   IMEM (do **NOT** move this)
  //   From IMEM
  //   Inputs/Outputs for testing. Do **NOT** move these.
  //   To DMEM
  //   DMEM (do **NOT** move this)
  //   From DMEM
endmodule
