// Logisim project imm-gen.circ as structural Verilog: 1 circuit, main circuit imm_gen
module imm_gen (
  input  [31:0] Instruction,
  input  [2:0] ImmSel,
  output [31:0] Immediate
);

  wire [31:0] Immediate_B, Immediate_I, Immediate_I2, Immediate_J, Immediate_S, Immediate_U;

  assign Immediate_U = {{12{Instruction[31]}}, Instruction[31:12]};  // Bit_Extender bit_extender_1
  assign Immediate_I = {{20{Instruction[31]}}, Instruction[31:20]};  // Bit_Extender bit_extender_2
  assign Immediate_I2 = {{27{Instruction[24]}}, Instruction[24:20]};  // Bit_Extender bit_extender_3
  assign Immediate_S = {{20{Instruction[31]}}, {Instruction[31:25], Instruction[11:7]}};  // Bit_Extender bit_extender_4
  assign Immediate_B = {{19{Instruction[31]}}, {Instruction[31], Instruction[7], Instruction[30:25], Instruction[11:8], Instruction[0]}};  // Bit_Extender bit_extender_5
  assign Immediate_J = {{11{Instruction[31]}}, {Instruction[31], Instruction[19:12], Instruction[20], Instruction[30:21], Instruction[0]}};  // Bit_Extender bit_extender_6
  Multiplexer #(.select(3), .width(32)) multiplexer_1 (
    .in0(Immediate_I), .in1(Immediate_S), .in2(Immediate_B), .in3(Immediate_U), .in4(Immediate_J),
    .out(Immediate), .sel(ImmSel));  // open: in5, in6, in7

  // Notes on the sheet:
  //   INPUTS to your circuit
  //   DON'T CHANGE THE LOCATIONS OF THE INPUTS AND OUTPUTS!
  //   OUTPUT from your circuit
endmodule
