// Logisim project partial-store.circ as structural Verilog: 1 circuit, main circuit partial_store
module partial_store (
  input  [31:0] Instruction,
  input  [31:0] MemAddress,
  input  [31:0] DataFromReg,
  input  MemWEn,
  output [3:0] MemWriteMask,
  output [31:0] DataToMem
);

  wire [3:0] bit_extender_7_out, multiplexer_6_out, SBMask, SHMask;
  wire [31:0] bit_extender_1_out, bit_extender_2_out, bit_extender_3_out, bit_extender_4_out,
       bit_extender_5_out, bit_extender_6_out, SBData, SBData1, SBData2, SBData3, SBData4, SHData, SHData1,
       SHData2;

  Multiplexer #(.select(3), .width(32)) multiplexer_1 (
    .in0(SBData), .in1(SHData), .in2(DataFromReg), .out(DataToMem), .sel(Instruction[14:12]));  // open: in3, in4, in5, in6, in7
  assign bit_extender_1_out = {{24{DataFromReg[7]}}, DataFromReg[7:0]};  // Bit_Extender bit_extender_1
  assign bit_extender_2_out = {{24{DataFromReg[7]}}, DataFromReg[7:0]};  // Bit_Extender bit_extender_2
  assign bit_extender_3_out = {{24{DataFromReg[7]}}, DataFromReg[7:0]};  // Bit_Extender bit_extender_3
  assign bit_extender_4_out = {{24{DataFromReg[7]}}, DataFromReg[7:0]};  // Bit_Extender bit_extender_4
  assign bit_extender_5_out = {{16{DataFromReg[15]}}, DataFromReg[15:0]};  // Bit_Extender bit_extender_5
  assign bit_extender_6_out = {{16{DataFromReg[15]}}, DataFromReg[15:0]};  // Bit_Extender bit_extender_6
  Shifter #(.width(32)) shifter_1 (.in(bit_extender_1_out), .\dist ({5{1'b0}}), .out(SBData1));
  Shifter #(.width(32)) shifter_2 (.in(bit_extender_2_out), .\dist (5'b01000), .out(SBData2));
  Shifter #(.width(32)) shifter_3 (.in(bit_extender_3_out), .\dist (5'b10000), .out(SBData3));
  Shifter #(.width(32)) shifter_4 (.in(bit_extender_4_out), .\dist (5'b11000), .out(SBData4));
  Shifter #(.width(32)) shifter_5 (.in(bit_extender_5_out), .\dist ({5{1'b0}}), .out(SHData1));
  Shifter #(.width(32)) shifter_6 (.in(bit_extender_6_out), .\dist (5'b10000), .out(SHData2));
  Multiplexer #(.select(2), .width(32)) multiplexer_2 (
    .in0(SHData1), .in2(SHData2), .out(SHData), .sel(MemAddress[1:0]));  // open: in1, in3
  Multiplexer #(.select(2), .width(32)) multiplexer_3 (
    .in0(SBData1), .in1(SBData2), .in2(SBData3), .in3(SBData4), .out(SBData), .sel(MemAddress[1:0]));
  Multiplexer #(.select(2), .width(4)) multiplexer_4 (
    .in0(4'b0001), .in1(4'b0010), .in2(4'b0100), .in3(4'b1000), .out(SBMask), .sel(MemAddress[1:0]));
  Multiplexer #(.select(2), .width(4)) multiplexer_5 (
    .in0(4'b0011), .in2(4'b1100), .out(SHMask), .sel(MemAddress[1:0]));  // open: in1, in3
  Multiplexer #(.select(3), .width(4)) multiplexer_6 (
    .in0(SBMask), .in1(SHMask), .in2(4'b1111), .out(multiplexer_6_out), .sel(Instruction[14:12]));  // open: in3, in4, in5, in6, in7
  assign bit_extender_7_out = {{3{MemWEn}}, MemWEn};  // Bit_Extender bit_extender_7
  assign MemWriteMask = bit_extender_7_out & multiplexer_6_out;  // AND_Gate and_1, 4 bits wide

  // Other names for the same wires on the sheet: NewDataFromReg[7:0] = DataFromReg[7:0];
  //   NewDataFromReg2[15:0] = DataFromReg[15:0]; SWData[31:0] = DataFromReg

  // Notes on the sheet:
  //   INPUTS to your circuit
  //   DON'T CHANGE THE LOCATIONS OF THE INPUTS AND OUTPUTS!
  //   OUTPUT from your circuit
endmodule
